// Logisim project Bocchino_Daniele_896187_arch1lab_progetto.circ as structural Verilog: 12 circuits, main circuit main
module main (
);

  wire and_1_out, barriers_1_gameover, clock, clock_1_out, comparator_1_eq, comparator_2_eq,
       controller_1_out_3, joystick_1_out_2, joystick_1_out_3, joystick_2_out_2, joystick_2_out_3, or_1_out,
       Reset;
  wire [1:0] X, Y;
  wire [4:0] counter_1_q, not_1_out, stop;
  wire [5:0] _1, _2, _3, _4, _5, _6, _7, _8, _9, _10, _11, _12, _13, _14, _15, _16, _17, _18, _19, _20, a, b,
       c, d, e, f, g, h, i, l, m, n, o, p, q, r, s, t, u, v;
  wire [31:0] barriers_1_out_35, barriers_1_out_36, barriers_1_out_37, barriers_1_out_38, barriers_1_out_39,
       barriers_1_out_40, barriers_1_out_41, barriers_1_out_42, barriers_1_out_43, barriers_1_out_44,
       barriers_1_out_45, barriers_1_out_46, barriers_1_out_47, barriers_1_out_48, barriers_1_out_49,
       barriers_1_out_50, barriers_1_out_51, barriers_1_out_52, barriers_1_out_53, barriers_1_out_54,
       barriers_1_out_55, barriers_1_out_56, barriers_1_out_57, barriers_1_out_58, barriers_1_out_59,
       barriers_1_out_60, barriers_1_out_61, barriers_1_out_62, barriers_1_out_63, barriers_1_out_65,
       barriers_1_out_66, barriers_1_out_67, decoder_1_out0, demultiplexer_1_out0, demultiplexer_1_out1,
       demultiplexer_1_out2, demultiplexer_1_out3, demultiplexer_1_out4, demultiplexer_1_out5,
       demultiplexer_1_out6, demultiplexer_1_out7, demultiplexer_1_out8, demultiplexer_1_out9,
       demultiplexer_1_out10, demultiplexer_1_out11, demultiplexer_1_out12, demultiplexer_1_out13,
       demultiplexer_1_out14, demultiplexer_1_out15, demultiplexer_1_out16, demultiplexer_1_out17,
       demultiplexer_1_out18, demultiplexer_1_out19, demultiplexer_1_out20, demultiplexer_1_out21,
       demultiplexer_1_out22, demultiplexer_1_out23, demultiplexer_1_out24, demultiplexer_1_out25,
       demultiplexer_1_out26, demultiplexer_1_out27, demultiplexer_1_out28, demultiplexer_1_out29,
       demultiplexer_1_out30, demultiplexer_1_out31;

  Clock clock_1 (.out(clock_1_out));
  Joystick joystick_1 (.in_1(X), .out_2(joystick_1_out_2), .out_3(joystick_1_out_3));
  Counter #(.width(5), .max('h1f), .ongoal("stay")) counter_1 (
    .load(joystick_1_out_2), .count(joystick_1_out_3), .Q(counter_1_q), .clk(and_1_out), .clr(Reset));  // open: D, carry
  Joystick joystick_2 (.in_1(Y), .out_2(joystick_2_out_2), .out_3(joystick_2_out_3));
  Counter #(.width(5), .max('h1f), .ongoal("stay"), .trigger("falling")) counter_2 (
    .load(joystick_2_out_2), .count(joystick_2_out_3), .Q(stop), .clk(and_1_out), .clr(Reset));  // open: D, carry
  and and_1 (and_1_out, clock_1_out, clock);
  assign not_1_out = ~counter_1_q;  // NOT_Gate not_1, 5 bits wide
  not not_2 (clock, barriers_1_gameover);
  Decoder #(.select(5), .enable("false")) decoder_1 (
    .out0(decoder_1_out0[0]), .out1(decoder_1_out0[1]), .out2(decoder_1_out0[2]), .out3(decoder_1_out0[3]),
    .out4(decoder_1_out0[4]), .out5(decoder_1_out0[5]), .out6(decoder_1_out0[6]), .out7(decoder_1_out0[7]),
    .out8(decoder_1_out0[8]), .out9(decoder_1_out0[9]), .out10(decoder_1_out0[10]),
    .out11(decoder_1_out0[11]), .out12(decoder_1_out0[12]), .out13(decoder_1_out0[13]),
    .out14(decoder_1_out0[14]), .out15(decoder_1_out0[15]), .out16(decoder_1_out0[16]),
    .out17(decoder_1_out0[17]), .out18(decoder_1_out0[18]), .out19(decoder_1_out0[19]),
    .out20(decoder_1_out0[20]), .out21(decoder_1_out0[21]), .out22(decoder_1_out0[22]),
    .out23(decoder_1_out0[23]), .out24(decoder_1_out0[24]), .out25(decoder_1_out0[25]),
    .out26(decoder_1_out0[26]), .out27(decoder_1_out0[27]), .out28(decoder_1_out0[28]),
    .out29(decoder_1_out0[29]), .out30(decoder_1_out0[30]), .out31(decoder_1_out0[31]), .sel(not_1_out));
  Demultiplexer #(.select(5), .width(32), .enable("false")) demultiplexer_1 (
    .out0(demultiplexer_1_out0), .out1(demultiplexer_1_out1), .out2(demultiplexer_1_out2),
    .out3(demultiplexer_1_out3), .out4(demultiplexer_1_out4), .out5(demultiplexer_1_out5),
    .out6(demultiplexer_1_out6), .out7(demultiplexer_1_out7), .out8(demultiplexer_1_out8),
    .out9(demultiplexer_1_out9), .out10(demultiplexer_1_out10), .out11(demultiplexer_1_out11),
    .out12(demultiplexer_1_out12), .out13(demultiplexer_1_out13), .out14(demultiplexer_1_out14),
    .out15(demultiplexer_1_out15), .out16(demultiplexer_1_out16), .out17(demultiplexer_1_out17),
    .out18(demultiplexer_1_out18), .out19(demultiplexer_1_out19), .out20(demultiplexer_1_out20),
    .out21(demultiplexer_1_out21), .out22(demultiplexer_1_out22), .out23(demultiplexer_1_out23),
    .out24(demultiplexer_1_out24), .out25(demultiplexer_1_out25), .out26(demultiplexer_1_out26),
    .out27(demultiplexer_1_out27), .out28(demultiplexer_1_out28), .out29(demultiplexer_1_out29),
    .out30(demultiplexer_1_out30), .out31(demultiplexer_1_out31), .in(decoder_1_out0), .sel(stop));
  Comparator #(.width(5)) comparator_1 (.a(stop), .b({5{1'b1}}), .eq(comparator_1_eq));  // open: gt, lt
  Comparator #(.width(5)) comparator_2 (.a(stop), .b({5{1'b0}}), .eq(comparator_2_eq));  // open: gt, lt
  barriers barriers_1 (
    .row_1(demultiplexer_1_out0), .row_2(demultiplexer_1_out1), .row_3(demultiplexer_1_out2),
    .row_4(demultiplexer_1_out3), .row_5(demultiplexer_1_out4), .row_6(demultiplexer_1_out5),
    .row_7(demultiplexer_1_out6), .row_8(demultiplexer_1_out7), .row_9(demultiplexer_1_out8),
    .row_10(demultiplexer_1_out9), .row_11(demultiplexer_1_out10), .row_12(demultiplexer_1_out11),
    .row_13(demultiplexer_1_out12), .row_14(demultiplexer_1_out13), .row_15(demultiplexer_1_out14),
    .row_16(demultiplexer_1_out15), .row_17(demultiplexer_1_out16), .row_18(demultiplexer_1_out17),
    .row_19(demultiplexer_1_out18), .row_20(demultiplexer_1_out19), .row_21(demultiplexer_1_out20),
    .row_22(demultiplexer_1_out21), .row_23(demultiplexer_1_out22), .row_24(demultiplexer_1_out23),
    .row_25(demultiplexer_1_out24), .row_26(demultiplexer_1_out25), .row_27(demultiplexer_1_out26),
    .row_28(demultiplexer_1_out27), .row_29(demultiplexer_1_out28), .row_30(demultiplexer_1_out29),
    .row_31(demultiplexer_1_out30), .row_32(demultiplexer_1_out31), .y(stop), .in_34(clock),
    .gameover(barriers_1_gameover), .out_35(barriers_1_out_35), .out_36(barriers_1_out_36),
    .out_37(barriers_1_out_37), .out_38(barriers_1_out_38), .out_39(barriers_1_out_39),
    .out_40(barriers_1_out_40), .out_41(barriers_1_out_41), .out_42(barriers_1_out_42),
    .out_43(barriers_1_out_43), .out_44(barriers_1_out_44), .out_45(barriers_1_out_45),
    .out_46(barriers_1_out_46), .out_47(barriers_1_out_47), .out_48(barriers_1_out_48),
    .out_49(barriers_1_out_49), .out_50(barriers_1_out_50), .out_51(barriers_1_out_51),
    .out_52(barriers_1_out_52), .out_53(barriers_1_out_53), .out_54(barriers_1_out_54),
    .out_55(barriers_1_out_55), .out_56(barriers_1_out_56), .out_57(barriers_1_out_57),
    .out_58(barriers_1_out_58), .out_59(barriers_1_out_59), .out_60(barriers_1_out_60),
    .out_61(barriers_1_out_61), .out_62(barriers_1_out_62), .out_63(barriers_1_out_63),
    .out_65(barriers_1_out_65), .out_66(barriers_1_out_66), .out_67(barriers_1_out_67));
  Controller controller_1 (.A(comparator_1_eq), .A_2(or_1_out), .out_3(controller_1_out_3));
  or or_1 (or_1_out, barriers_1_gameover, comparator_2_eq);
  DotMatrix #(.inputtype("row"), .matrixcols(32), .matrixrows(32)) dotmatrix_1 (
    .row0(barriers_1_out_35), .row1(barriers_1_out_36), .row2(barriers_1_out_37), .row3(barriers_1_out_38),
    .row4(barriers_1_out_39), .row5(barriers_1_out_40), .row6(barriers_1_out_41), .row7(barriers_1_out_42),
    .row8(barriers_1_out_43), .row9(barriers_1_out_44), .row10(barriers_1_out_45), .row11(barriers_1_out_46),
    .row12(barriers_1_out_47), .row13(barriers_1_out_48), .row14(barriers_1_out_49),
    .row15(barriers_1_out_50), .row16(barriers_1_out_51), .row17(barriers_1_out_52),
    .row18(barriers_1_out_53), .row19(barriers_1_out_54), .row20(barriers_1_out_55),
    .row21(barriers_1_out_56), .row22(barriers_1_out_57), .row23(barriers_1_out_58),
    .row24(barriers_1_out_59), .row25(barriers_1_out_60), .row26(barriers_1_out_61),
    .row27(barriers_1_out_62), .row28(barriers_1_out_63), .row29(barriers_1_out_65),
    .row30(barriers_1_out_66), .row31(barriers_1_out_67));
  DotMatrix #(.matrixcols(20), .matrixrows(6)) dotmatrix_2 (
    .col0(_1), .col1(_2), .col2(_3), .col3(_4), .col4(_5), .col5(_6), .col6(_7), .col7(_8), .col8(_9),
    .col9(_10), .col10(_11), .col11(_12), .col12(_13), .col13(_14), .col14(_15), .col15(_16), .col16(_17),
    .col17(_18), .col18(_19), .col19(_20));
  Empty empty_1 (
    .I(controller_1_out_3), .out_3(_1), .out_4(_2), .out_5(_3), .out_6(_4), .out_7(_5), .out_8(_6),
    .out_9(_7), .out_10(_8), .out_11(_9), .out_12(_10), .out_13(_11), .out_14(_12), .out_15(_13),
    .out_16(_14), .out_17(_15), .out_18(_16), .out_19(_17), .out_20(_18), .out_21(_19), .out_22(_20),
    .out_23(a), .out_24(b), .out_25(c), .out_26(d), .out_27(e), .out_28(f), .out_29(g), .out_30(h),
    .out_31(i), .out_32(l), .out_33(m), .out_34(n), .out_35(o), .out_36(p), .out_37(q), .out_38(r),
    .out_39(s), .out_40(t), .out_41(u), .out_42(v));  // open: clear
  Win win_1 (
    .I(comparator_1_eq), .clear(Reset), .out_3(_1), .out_4(_2), .out_5(_3), .out_6(_4), .out_7(_5),
    .out_8(_6), .out_9(_7), .out_10(_8), .out_11(_9), .out_12(_10), .out_13(_11), .out_14(_12), .out_15(_13),
    .out_16(_14), .out_17(_15), .out_18(_16), .out_19(_17), .out_20(_18), .out_21(_19), .out_22(_20),
    .out_23(a), .out_24(b), .out_25(c), .out_26(d), .out_27(e), .out_28(f), .out_29(g), .out_30(h),
    .out_31(i), .out_32(l), .out_33(m), .out_34(n), .out_35(o), .out_36(p), .out_37(q), .out_38(r),
    .out_39(s), .out_40(t), .out_41(u), .out_42(v));
  Game_Over game_over_1 (
    .I(or_1_out), .clear(Reset), .out_3(_1), .out_4(_2), .out_5(_3), .out_6(_4), .out_7(_5), .out_8(_6),
    .out_9(_7), .out_10(_8), .out_11(_9), .out_12(_10), .out_13(_11), .out_14(_12), .out_15(_13),
    .out_16(_14), .out_17(_15), .out_18(_16), .out_19(_17), .out_20(_18), .out_21(_19), .out_22(_20),
    .out_23(a), .out_24(b), .out_25(c), .out_26(d), .out_27(e), .out_28(f), .out_29(g), .out_30(h),
    .out_31(i), .out_32(l), .out_33(m), .out_34(n), .out_35(o), .out_36(p), .out_37(q), .out_38(r),
    .out_39(s), .out_40(t), .out_41(u), .out_42(v));
  DotMatrix #(.matrixcols(20), .matrixrows(6)) dotmatrix_3 (
    .col0(a), .col1(b), .col2(c), .col3(d), .col4(e), .col5(f), .col6(g), .col7(h), .col8(i), .col9(l),
    .col10(m), .col11(n), .col12(o), .col13(p), .col14(q), .col15(r), .col16(s), .col17(t), .col18(u),
    .col19(v));
  Button Reset_Botton (.out(Reset));
  Joystick_part #(.bits(2)) joystick_3 (.x(X), .y(Y));

  // Notes on the sheet:
  //   ISTRUZIONI
  //   Lo Scopo del gioco è raggiungere il
  //   fondo della matrice con la pallina
  //   Per farlo l'utente dovrà 
  //   utilizzare il Joystick per  muoversi
  //   in caso di Game Over  sarà
  //   necessario premere " Reset Botton"
  //   per avviare una nuova partita.
  //   Joystick
endmodule

// Barriers
module barriers (
  input  [31:0] row_1,
  input  [31:0] row_2,
  input  [31:0] row_3,
  input  [31:0] row_4,
  input  [31:0] row_5,
  input  [31:0] row_6,
  input  [31:0] row_7,
  input  [31:0] row_8,
  input  [31:0] row_9,
  input  [31:0] row_10,
  input  [31:0] row_11,
  input  [31:0] row_12,
  input  [31:0] row_13,
  input  [31:0] row_14,
  input  [31:0] row_15,
  input  [31:0] row_16,
  input  [31:0] row_17,
  input  [31:0] row_18,
  input  [31:0] row_19,
  input  [31:0] row_20,
  input  [31:0] row_21,
  input  [31:0] row_22,
  input  [31:0] row_23,
  input  [31:0] row_24,
  input  [31:0] row_25,
  input  [31:0] row_26,
  input  [31:0] row_27,
  input  [31:0] row_28,
  input  [31:0] row_29,
  input  [31:0] row_30,
  input  [31:0] row_31,
  input  [4:0] y,
  input  [31:0] row_32,
  input  in_34,
  output [31:0] out_35,
  output [31:0] out_36,
  output [31:0] out_37,
  output [31:0] out_38,
  output [31:0] out_39,
  output [31:0] out_40,
  output [31:0] out_41,
  output [31:0] out_42,
  output [31:0] out_43,
  output [31:0] out_44,
  output [31:0] out_45,
  output [31:0] out_46,
  output [31:0] out_47,
  output [31:0] out_48,
  output [31:0] out_49,
  output [31:0] out_50,
  output [31:0] out_51,
  output [31:0] out_52,
  output [31:0] out_53,
  output [31:0] out_54,
  output [31:0] out_55,
  output [31:0] out_56,
  output [31:0] out_57,
  output [31:0] out_58,
  output [31:0] out_59,
  output [31:0] out_60,
  output [31:0] out_61,
  output [31:0] out_62,
  output [31:0] out_63,
  output gameover,
  output [31:0] out_65,
  output [31:0] out_66,
  output [31:0] out_67
);

  wire a_1_game_over, b_1_game_over, b_2_game_over, d_1_out_4, d_2_out_4, f_1_out_4, f_2_out_4, f_3_out_4,
       f_4_out_4;

  D d_1 (.Clock(in_34), .b(row_3), .c(out_37), .out_4(d_1_out_4));
  F f_1 (.Clock(in_34), .b(row_6), .c(out_40), .out_4(f_1_out_4));
  B b_1 (.Clock(in_34), .b(row_10), .c(out_44), .Game_Over(b_1_game_over));
  F f_2 (.Clock(in_34), .b(row_13), .c(out_47), .out_4(f_2_out_4));
  A a_1 (.Clock(in_34), .b(row_16), .c(out_50), .Game_Over(a_1_game_over));
  F f_3 (.Clock(in_34), .b(row_19), .c(out_53), .out_4(f_3_out_4));
  B b_2 (.Clock(in_34), .b(row_22), .c(out_56), .Game_Over(b_2_game_over));
  F f_4 (.Clock(in_34), .b(row_26), .c(out_60), .out_4(f_4_out_4));
  D d_2 (.Clock(in_34), .b(row_30), .c(out_65), .out_4(d_2_out_4));
  Multiplexer #(.select(5)) multiplexer_1 (
    .in0(1'b0), .in1(1'b0), .in2(d_1_out_4), .in3(1'b0), .in4(1'b0), .in5(f_1_out_4), .in6(1'b0), .in7(1'b0),
    .in8(1'b0), .in9(b_1_game_over), .in10(1'b0), .in11(1'b0), .in12(f_2_out_4), .in13(1'b0), .in14(1'b0),
    .in15(a_1_game_over), .in16(1'b0), .in17(1'b0), .in18(f_3_out_4), .in19(1'b0), .in20(1'b0),
    .in21(b_2_game_over), .in22(1'b0), .in23(1'b0), .in24(1'b0), .in25(f_4_out_4), .in26(1'b0), .in27(1'b0),
    .in28(1'b0), .in29(d_2_out_4), .in30(1'b0), .in31(1'b0), .out(gameover), .sel(y));  // open: en

  assign out_35 = row_1;
  assign out_36 = row_2;
  assign out_38 = row_4;
  assign out_39 = row_5;
  assign out_41 = row_7;
  assign out_42 = row_8;
  assign out_43 = row_9;
  assign out_45 = row_11;
  assign out_46 = row_12;
  assign out_48 = row_14;
  assign out_49 = row_15;
  assign out_51 = row_17;
  assign out_52 = row_18;
  assign out_54 = row_20;
  assign out_55 = row_21;
  assign out_57 = row_23;
  assign out_58 = row_24;
  assign out_59 = row_25;
  assign out_61 = row_27;
  assign out_62 = row_28;
  assign out_63 = row_29;
  assign out_66 = row_31;
  assign out_67 = row_32;

  // Other names for the same wires on the sheet: clock = in_34
endmodule

module A (
  input  Clock,
  input  [31:0] b,
  output [31:0] c,
  output Game_Over
);

  wire and_1_out, clock_1_out;
  wire [2:0] counter_1_q;
  wire [31:0] rom_1_data;

  Clock #(.highDuration(5), .lowDuration(5)) clock_1 (.out(clock_1_out));
  and and_1 (and_1_out, clock_1_out, Clock);
  Counter #(.width(3), .max('h7)) counter_1 (
    .count(and_1_out), .Q(counter_1_q), .clk(and_1_out));  // open: load, D, carry, clr
  ROM #(.addrWidth(3), .dataWidth(32)) rom_1 (.addr(counter_1_q), .data(rom_1_data));  // open: sel
  assign c = rom_1_data | b;  // OR_Gate or_1, 32 bits wide
  Comparator #(.width(32)) comparator_1 (.a(c), .b(rom_1_data), .eq(Game_Over));  // open: gt, lt

  // Notes on the sheet:
  //   contents of rom_1 (hex, n*v repeats v):
  //   44444444 44444444 44444444 22222222 11111111 11111111 22222222 22222222
endmodule

module B (
  input  Clock,
  input  [31:0] b,
  output [31:0] c,
  output Game_Over
);

  wire and_1_out, clock_1_out;
  wire [2:0] counter_1_q;
  wire [31:0] rom_1_data;

  Clock #(.highDuration(4), .lowDuration(7)) clock_1 (.out(clock_1_out));
  and and_1 (and_1_out, clock_1_out, Clock);
  Counter #(.width(3), .max('h7)) counter_1 (
    .count(and_1_out), .Q(counter_1_q), .clk(and_1_out));  // open: load, D, carry, clr
  ROM #(.addrWidth(3), .dataWidth(32)) rom_1 (.addr(counter_1_q), .data(rom_1_data));  // open: sel
  Comparator #(.width(32)) comparator_1 (.a(c), .b(rom_1_data), .eq(Game_Over));  // open: gt, lt
  assign c = rom_1_data | b;  // OR_Gate or_1, 32 bits wide

  // Notes on the sheet:
  //   contents of rom_1 (hex, n*v repeats v):
  //   10101010 1010101 10101010 1010101 10101010 1010101 10101010 1010101
endmodule

module D (
  input  Clock,
  input  [31:0] b,
  output [31:0] c,
  output out_4
);

  wire and_1_out, clock_1_out;
  wire [2:0] counter_1_q;
  wire [31:0] rom_1_data;

  Clock #(.highDuration(5), .lowDuration(15)) clock_1 (.out(clock_1_out));
  and and_1 (and_1_out, clock_1_out, Clock);
  Counter #(.width(3), .max('h7)) counter_1 (
    .count(and_1_out), .Q(counter_1_q), .clk(and_1_out));  // open: load, D, carry, clr
  ROM #(.addrWidth(3), .dataWidth(32)) rom_1 (.addr(counter_1_q), .data(rom_1_data));  // open: sel
  Comparator #(.width(32)) comparator_1 (.a(rom_1_data), .b(c), .eq(out_4));  // open: gt, lt
  assign c = rom_1_data | b;  // OR_Gate or_1, 32 bits wide

  // Notes on the sheet:
  //   contents of rom_1 (hex, n*v repeats v):
  //   8*77777777
endmodule

module F (
  input  Clock,
  input  [31:0] b,
  output [31:0] c,
  output out_4
);

  wire and_1_out, clock_1_out;
  wire [2:0] counter_1_q;
  wire [31:0] rom_1_data;

  Clock #(.highDuration(2), .lowDuration(15)) clock_1 (.out(clock_1_out));
  and and_1 (and_1_out, clock_1_out, Clock);
  Counter #(.width(3), .max('h7)) counter_1 (
    .count(and_1_out), .Q(counter_1_q), .clk(and_1_out));  // open: load, D, carry, clr
  ROM #(.addrWidth(3), .dataWidth(32)) rom_1 (.addr(counter_1_q), .data(rom_1_data));  // open: sel
  assign c = rom_1_data | b;  // OR_Gate or_1, 32 bits wide
  Comparator #(.width(32)) comparator_1 (.a(rom_1_data), .b(c), .eq(out_4));  // open: gt, lt

  // Notes on the sheet:
  //   contents of rom_1 (hex, n*v repeats v):
  //   33333333 0 33333333 0 33333333 0 33333333
endmodule

// Joy
module Joystick (
  input  [1:0] in_1,
  output out_2,
  output out_3
);

  wire comparator_2_eq;

  Comparator #(.width(2)) comparator_1 (.a(in_1), .b(2'b01), .eq(out_2));  // open: gt, lt
  Comparator #(.width(2)) comparator_2 (.a(in_1), .b(2'b11), .eq(comparator_2_eq));  // open: gt, lt
  or or_1 (out_3, out_2, comparator_2_eq);
endmodule

// Game Over Matrix
module Game_Over (
  input  I,
  input  clear,
  output [5:0] out_3,
  output [5:0] out_4,
  output [5:0] out_5,
  output [5:0] out_6,
  output [5:0] out_7,
  output [5:0] out_8,
  output [5:0] out_9,
  output [5:0] out_10,
  output [5:0] out_11,
  output [5:0] out_12,
  output [5:0] out_13,
  output [5:0] out_14,
  output [5:0] out_15,
  output [5:0] out_16,
  output [5:0] out_17,
  output [5:0] out_18,
  output [5:0] out_19,
  output [5:0] out_20,
  output [5:0] out_21,
  output [5:0] out_22,
  output [5:0] out_23,
  output [5:0] out_24,
  output [5:0] out_25,
  output [5:0] out_26,
  output [5:0] out_27,
  output [5:0] out_28,
  output [5:0] out_29,
  output [5:0] out_30,
  output [5:0] out_31,
  output [5:0] out_32,
  output [5:0] out_33,
  output [5:0] out_34,
  output [5:0] out_35,
  output [5:0] out_36,
  output [5:0] out_37,
  output [5:0] out_38,
  output [5:0] out_39,
  output [5:0] out_40,
  output [5:0] out_41,
  output [5:0] out_42
);

  wire [1:0] counter_1_out_3;

  counter counter_1 (.I(I), .clear(clear), .out_3(counter_1_out_3));
  ROM #(.addrWidth(2), .dataWidth(6)) rom_1 (.addr(counter_1_out_3), .data(out_3), .sel(I));
  ROM #(.addrWidth(2), .dataWidth(6)) rom_2 (.addr(counter_1_out_3), .data(out_4), .sel(I));
  ROM #(.addrWidth(2), .dataWidth(6)) rom_3 (.addr(counter_1_out_3), .data(out_5), .sel(I));
  ROM #(.addrWidth(2), .dataWidth(6)) rom_4 (.addr(counter_1_out_3), .data(out_6), .sel(I));
  ROM #(.addrWidth(2), .dataWidth(6)) rom_5 (.addr(counter_1_out_3), .data(out_7), .sel(I));
  ROM #(.addrWidth(2), .dataWidth(6)) rom_6 (.addr(counter_1_out_3), .data(out_8), .sel(I));
  ROM #(.addrWidth(2), .dataWidth(6)) rom_7 (.addr(counter_1_out_3), .data(out_9), .sel(I));
  ROM #(.addrWidth(2), .dataWidth(6)) rom_8 (.addr(counter_1_out_3), .data(out_10), .sel(I));
  ROM #(.addrWidth(2), .dataWidth(6)) rom_9 (.addr(counter_1_out_3), .data(out_11), .sel(I));
  ROM #(.addrWidth(2), .dataWidth(6)) rom_10 (.addr(counter_1_out_3), .data(out_12), .sel(I));
  ROM #(.addrWidth(2), .dataWidth(6)) rom_11 (.addr(counter_1_out_3), .data(out_13), .sel(I));
  ROM #(.addrWidth(2), .dataWidth(6)) rom_12 (.addr(counter_1_out_3), .data(out_14), .sel(I));
  ROM #(.addrWidth(2), .dataWidth(6)) rom_13 (.addr(counter_1_out_3), .data(out_15), .sel(I));
  ROM #(.addrWidth(2), .dataWidth(6)) rom_14 (.addr(counter_1_out_3), .data(out_16), .sel(I));
  ROM #(.addrWidth(2), .dataWidth(6)) rom_15 (.addr(counter_1_out_3), .data(out_17), .sel(I));
  ROM #(.addrWidth(2), .dataWidth(6)) rom_16 (.addr(counter_1_out_3), .data(out_18), .sel(I));
  ROM #(.addrWidth(2), .dataWidth(6)) rom_17 (.addr(counter_1_out_3), .data(out_19), .sel(I));
  ROM #(.addrWidth(2), .dataWidth(6)) rom_18 (.addr(counter_1_out_3), .data(out_20), .sel(I));
  ROM #(.addrWidth(2), .dataWidth(6)) rom_19 (.addr(counter_1_out_3), .data(out_21), .sel(I));
  ROM #(.addrWidth(2), .dataWidth(6)) rom_20 (.addr(counter_1_out_3), .data(out_22), .sel(I));
  ROM #(.addrWidth(2), .dataWidth(6)) rom_21 (.addr(counter_1_out_3), .data(out_23), .sel(I));
  ROM #(.addrWidth(2), .dataWidth(6)) rom_22 (.addr(counter_1_out_3), .data(out_24), .sel(I));
  ROM #(.addrWidth(2), .dataWidth(6)) rom_23 (.addr(counter_1_out_3), .data(out_25), .sel(I));
  ROM #(.addrWidth(2), .dataWidth(6)) rom_24 (.addr(counter_1_out_3), .data(out_26), .sel(I));
  ROM #(.addrWidth(2), .dataWidth(6)) rom_25 (.addr(counter_1_out_3), .data(out_27), .sel(I));
  ROM #(.addrWidth(2), .dataWidth(6)) rom_26 (.addr(counter_1_out_3), .data(out_28), .sel(I));
  ROM #(.addrWidth(2), .dataWidth(6)) rom_27 (.addr(counter_1_out_3), .data(out_29), .sel(I));
  ROM #(.addrWidth(2), .dataWidth(6)) rom_28 (.addr(counter_1_out_3), .data(out_30), .sel(I));
  ROM #(.addrWidth(2), .dataWidth(6)) rom_29 (.addr(counter_1_out_3), .data(out_31), .sel(I));
  ROM #(.addrWidth(2), .dataWidth(6)) rom_30 (.addr(counter_1_out_3), .data(out_32), .sel(I));
  ROM #(.addrWidth(2), .dataWidth(6)) rom_31 (.addr(counter_1_out_3), .data(out_33), .sel(I));
  ROM #(.addrWidth(2), .dataWidth(6)) rom_32 (.addr(counter_1_out_3), .data(out_34), .sel(I));
  ROM #(.addrWidth(2), .dataWidth(6)) rom_33 (.addr(counter_1_out_3), .data(out_35), .sel(I));
  ROM #(.addrWidth(2), .dataWidth(6)) rom_34 (.addr(counter_1_out_3), .data(out_36), .sel(I));
  ROM #(.addrWidth(2), .dataWidth(6)) rom_35 (.addr(counter_1_out_3), .data(out_37), .sel(I));
  ROM #(.addrWidth(2), .dataWidth(6)) rom_36 (.addr(counter_1_out_3), .data(out_38), .sel(I));
  ROM #(.addrWidth(2), .dataWidth(6)) rom_37 (.addr(counter_1_out_3), .data(out_39), .sel(I));
  ROM #(.addrWidth(2), .dataWidth(6)) rom_38 (.addr(counter_1_out_3), .data(out_40), .sel(I));
  ROM #(.addrWidth(2), .dataWidth(6)) rom_39 (.addr(counter_1_out_3), .data(out_41), .sel(I));
  ROM #(.addrWidth(2), .dataWidth(6)) rom_40 (.addr(counter_1_out_3), .data(out_42), .sel(I));

  // Notes on the sheet:
  //   contents of rom_1 (hex, n*v repeats v):
  //   3f 3f
  //   contents of rom_2 (hex, n*v repeats v):
  //   28 21
  //   contents of rom_3 (hex, n*v repeats v):
  //   28 25
  //   contents of rom_4 (hex, n*v repeats v):
  //   38 27
  //   contents of rom_6 (hex, n*v repeats v):
  //   3f 3f
  //   contents of rom_7 (hex, n*v repeats v):
  //   1 24
  //   contents of rom_8 (hex, n*v repeats v):
  //   1 24
  //   contents of rom_9 (hex, n*v repeats v):
  //   0 3f
  //   contents of rom_10 (hex, n*v repeats v):
  //   3f
  //   contents of rom_11 (hex, n*v repeats v):
  //   24 3f
  //   contents of rom_12 (hex, n*v repeats v):
  //   24 10
  //   contents of rom_13 (hex, n*v repeats v):
  //   3f 8
  //   contents of rom_14 (hex, n*v repeats v):
  //   0 10
  //   contents of rom_15 (hex, n*v repeats v):
  //   30 3f
  //   contents of rom_16 (hex, n*v repeats v):
  //   8
  //   contents of rom_17 (hex, n*v repeats v):
  //   7 3f
  //   contents of rom_18 (hex, n*v repeats v):
  //   8 25
  //   contents of rom_19 (hex, n*v repeats v):
  //   30 25
  //   contents of rom_20 (hex, n*v repeats v):
  //   0 21
  //   contents of rom_21 (hex, n*v repeats v):
  //   3f 3f
  //   contents of rom_22 (hex, n*v repeats v):
  //   21 21
  //   contents of rom_23 (hex, n*v repeats v):
  //   25 21
  //   contents of rom_24 (hex, n*v repeats v):
  //   27 3f
  //   contents of rom_26 (hex, n*v repeats v):
  //   3f 3c
  //   contents of rom_27 (hex, n*v repeats v):
  //   24 2
  //   contents of rom_28 (hex, n*v repeats v):
  //   24 1
  //   contents of rom_29 (hex, n*v repeats v):
  //   3f 2
  //   contents of rom_30 (hex, n*v repeats v):
  //   0 3c
  //   contents of rom_31 (hex, n*v repeats v):
  //   3f
  //   contents of rom_32 (hex, n*v repeats v):
  //   10 3f
  //   contents of rom_33 (hex, n*v repeats v):
  //   8 25
  //   contents of rom_34 (hex, n*v repeats v):
  //   10 21
  //   contents of rom_35 (hex, n*v repeats v):
  //   3f
  //   contents of rom_36 (hex, n*v repeats v):
  //   0 3f
  //   contents of rom_37 (hex, n*v repeats v):
  //   3f 24
  //   contents of rom_38 (hex, n*v repeats v):
  //   25 24
  //   contents of rom_39 (hex, n*v repeats v):
  //   25 1a
  //   contents of rom_40 (hex, n*v repeats v):
  //   21 1
endmodule

module counter (
  input  I,
  input  clear,
  output [1:0] out_3
);

  wire and_1_out, register_1_q;

  and and_1 (and_1_out, 1'b1, I);
  Register #(.width(1)) register_1 (.D(I), .en(and_1_out), .Q(register_1_q), .clk(and_1_out), .clr(clear));
  assign out_3 = {{1{1'b0}}, register_1_q};  // Bit_Extender bit_extender_1
endmodule

// Win Matrix
module Win (
  input  I,
  input  clear,
  output [5:0] out_3,
  output [5:0] out_4,
  output [5:0] out_5,
  output [5:0] out_6,
  output [5:0] out_7,
  output [5:0] out_8,
  output [5:0] out_9,
  output [5:0] out_10,
  output [5:0] out_11,
  output [5:0] out_12,
  output [5:0] out_13,
  output [5:0] out_14,
  output [5:0] out_15,
  output [5:0] out_16,
  output [5:0] out_17,
  output [5:0] out_18,
  output [5:0] out_19,
  output [5:0] out_20,
  output [5:0] out_21,
  output [5:0] out_22,
  output [5:0] out_23,
  output [5:0] out_24,
  output [5:0] out_25,
  output [5:0] out_26,
  output [5:0] out_27,
  output [5:0] out_28,
  output [5:0] out_29,
  output [5:0] out_30,
  output [5:0] out_31,
  output [5:0] out_32,
  output [5:0] out_33,
  output [5:0] out_34,
  output [5:0] out_35,
  output [5:0] out_36,
  output [5:0] out_37,
  output [5:0] out_38,
  output [5:0] out_39,
  output [5:0] out_40,
  output [5:0] out_41,
  output [5:0] out_42
);

  wire [1:0] counter_1_out_3;

  counter counter_1 (.I(I), .clear(clear), .out_3(counter_1_out_3));
  ROM #(.addrWidth(2), .dataWidth(6)) rom_1 (.addr(counter_1_out_3), .data(out_3), .sel(I));
  ROM #(.addrWidth(2), .dataWidth(6)) rom_2 (.addr(counter_1_out_3), .data(out_4), .sel(I));
  ROM #(.addrWidth(2), .dataWidth(6)) rom_3 (.addr(counter_1_out_3), .data(out_5), .sel(I));
  ROM #(.addrWidth(2), .dataWidth(6)) rom_4 (.addr(counter_1_out_3), .data(out_6), .sel(I));
  ROM #(.addrWidth(2), .dataWidth(6)) rom_5 (.addr(counter_1_out_3), .data(out_7), .sel(I));
  ROM #(.addrWidth(2), .dataWidth(6)) rom_6 (.addr(counter_1_out_3), .data(out_8), .sel(I));
  ROM #(.addrWidth(2), .dataWidth(6)) rom_7 (.addr(counter_1_out_3), .data(out_9), .sel(I));
  ROM #(.addrWidth(2), .dataWidth(6)) rom_8 (.addr(counter_1_out_3), .data(out_10), .sel(I));
  ROM #(.addrWidth(2), .dataWidth(6)) rom_9 (.addr(counter_1_out_3), .data(out_11), .sel(I));
  ROM #(.addrWidth(2), .dataWidth(6)) rom_10 (.addr(counter_1_out_3), .data(out_12), .sel(I));
  ROM #(.addrWidth(2), .dataWidth(6)) rom_11 (.addr(counter_1_out_3), .data(out_13), .sel(I));
  ROM #(.addrWidth(2), .dataWidth(6)) rom_12 (.addr(counter_1_out_3), .data(out_14), .sel(I));
  ROM #(.addrWidth(2), .dataWidth(6)) rom_13 (.addr(counter_1_out_3), .data(out_15), .sel(I));
  ROM #(.addrWidth(2), .dataWidth(6)) rom_14 (.addr(counter_1_out_3), .data(out_16), .sel(I));
  ROM #(.addrWidth(2), .dataWidth(6)) rom_15 (.addr(counter_1_out_3), .data(out_17), .sel(I));
  ROM #(.addrWidth(2), .dataWidth(6)) rom_16 (.addr(counter_1_out_3), .data(out_18), .sel(I));
  ROM #(.addrWidth(2), .dataWidth(6)) rom_17 (.addr(counter_1_out_3), .data(out_19), .sel(I));
  ROM #(.addrWidth(2), .dataWidth(6)) rom_18 (.addr(counter_1_out_3), .data(out_20), .sel(I));
  ROM #(.addrWidth(2), .dataWidth(6)) rom_19 (.addr(counter_1_out_3), .data(out_21), .sel(I));
  ROM #(.addrWidth(2), .dataWidth(6)) rom_20 (.addr(counter_1_out_3), .data(out_22), .sel(I));
  ROM #(.addrWidth(2), .dataWidth(6)) rom_21 (.addr(counter_1_out_3), .data(out_23), .sel(I));
  ROM #(.addrWidth(2), .dataWidth(6)) rom_22 (.addr(counter_1_out_3), .data(out_24), .sel(I));
  ROM #(.addrWidth(2), .dataWidth(6)) rom_23 (.addr(counter_1_out_3), .data(out_25), .sel(I));
  ROM #(.addrWidth(2), .dataWidth(6)) rom_24 (.addr(counter_1_out_3), .data(out_26), .sel(I));
  ROM #(.addrWidth(2), .dataWidth(6)) rom_25 (.addr(counter_1_out_3), .data(out_27), .sel(I));
  ROM #(.addrWidth(2), .dataWidth(6)) rom_26 (.addr(counter_1_out_3), .data(out_28), .sel(I));
  ROM #(.addrWidth(2), .dataWidth(6)) rom_27 (.addr(counter_1_out_3), .data(out_29), .sel(I));
  ROM #(.addrWidth(2), .dataWidth(6)) rom_28 (.addr(counter_1_out_3), .data(out_30), .sel(I));
  ROM #(.addrWidth(2), .dataWidth(6)) rom_29 (.addr(counter_1_out_3), .data(out_31), .sel(I));
  ROM #(.addrWidth(2), .dataWidth(6)) rom_30 (.addr(counter_1_out_3), .data(out_32), .sel(I));
  ROM #(.addrWidth(2), .dataWidth(6)) rom_31 (.addr(counter_1_out_3), .data(out_33), .sel(I));
  ROM #(.addrWidth(2), .dataWidth(6)) rom_32 (.addr(counter_1_out_3), .data(out_34), .sel(I));
  ROM #(.addrWidth(2), .dataWidth(6)) rom_33 (.addr(counter_1_out_3), .data(out_35), .sel(I));
  ROM #(.addrWidth(2), .dataWidth(6)) rom_34 (.addr(counter_1_out_3), .data(out_36), .sel(I));
  ROM #(.addrWidth(2), .dataWidth(6)) rom_35 (.addr(counter_1_out_3), .data(out_37), .sel(I));
  ROM #(.addrWidth(2), .dataWidth(6)) rom_36 (.addr(counter_1_out_3), .data(out_38), .sel(I));
  ROM #(.addrWidth(2), .dataWidth(6)) rom_37 (.addr(counter_1_out_3), .data(out_39), .sel(I));
  ROM #(.addrWidth(2), .dataWidth(6)) rom_38 (.addr(counter_1_out_3), .data(out_40), .sel(I));
  ROM #(.addrWidth(2), .dataWidth(6)) rom_39 (.addr(counter_1_out_3), .data(out_41), .sel(I));
  ROM #(.addrWidth(2), .dataWidth(6)) rom_40 (.addr(counter_1_out_3), .data(out_42), .sel(I));

  // Notes on the sheet:
  //   contents of rom_3 (hex, n*v repeats v):
  //   4*30
  //   contents of rom_4 (hex, n*v repeats v):
  //   4*8
  //   contents of rom_5 (hex, n*v repeats v):
  //   4*7
  //   contents of rom_6 (hex, n*v repeats v):
  //   4*8
  //   contents of rom_7 (hex, n*v repeats v):
  //   4*30
  //   contents of rom_9 (hex, n*v repeats v):
  //   4*3f
  //   contents of rom_10 (hex, n*v repeats v):
  //   4*21
  //   contents of rom_11 (hex, n*v repeats v):
  //   4*21
  //   contents of rom_12 (hex, n*v repeats v):
  //   4*3f
  //   contents of rom_14 (hex, n*v repeats v):
  //   4*3f
  //   contents of rom_15 (hex, n*v repeats v):
  //   4*1
  //   contents of rom_16 (hex, n*v repeats v):
  //   4*1
  //   contents of rom_17 (hex, n*v repeats v):
  //   4*3f
  //   contents of rom_23 (hex, n*v repeats v):
  //   4*3c
  //   contents of rom_24 (hex, n*v repeats v):
  //   4*2
  //   contents of rom_25 (hex, n*v repeats v):
  //   4*1
  //   contents of rom_26 (hex, n*v repeats v):
  //   4*7
  //   contents of rom_27 (hex, n*v repeats v):
  //   4*1
  //   contents of rom_28 (hex, n*v repeats v):
  //   4*2
  //   contents of rom_29 (hex, n*v repeats v):
  //   4*3c
  //   contents of rom_31 (hex, n*v repeats v):
  //   4*3f
  //   contents of rom_33 (hex, n*v repeats v):
  //   4*3f
  //   contents of rom_34 (hex, n*v repeats v):
  //   4*10
  //   contents of rom_35 (hex, n*v repeats v):
  //   4*8
  //   contents of rom_36 (hex, n*v repeats v):
  //   4*4
  //   contents of rom_37 (hex, n*v repeats v):
  //   4*3f
  //   contents of rom_39 (hex, n*v repeats v):
  //   4*3d
endmodule

// Empty Matrix
module Empty (
  input  I,
  input  clear,
  output [5:0] out_3,
  output [5:0] out_4,
  output [5:0] out_5,
  output [5:0] out_6,
  output [5:0] out_7,
  output [5:0] out_8,
  output [5:0] out_9,
  output [5:0] out_10,
  output [5:0] out_11,
  output [5:0] out_12,
  output [5:0] out_13,
  output [5:0] out_14,
  output [5:0] out_15,
  output [5:0] out_16,
  output [5:0] out_17,
  output [5:0] out_18,
  output [5:0] out_19,
  output [5:0] out_20,
  output [5:0] out_21,
  output [5:0] out_22,
  output [5:0] out_23,
  output [5:0] out_24,
  output [5:0] out_25,
  output [5:0] out_26,
  output [5:0] out_27,
  output [5:0] out_28,
  output [5:0] out_29,
  output [5:0] out_30,
  output [5:0] out_31,
  output [5:0] out_32,
  output [5:0] out_33,
  output [5:0] out_34,
  output [5:0] out_35,
  output [5:0] out_36,
  output [5:0] out_37,
  output [5:0] out_38,
  output [5:0] out_39,
  output [5:0] out_40,
  output [5:0] out_41,
  output [5:0] out_42
);

  wire [1:0] counter_1_out_3;

  counter counter_1 (.I(I), .clear(clear), .out_3(counter_1_out_3));
  ROM #(.addrWidth(2), .dataWidth(6)) rom_1 (.addr(counter_1_out_3), .data(out_3), .sel(I));
  ROM #(.addrWidth(2), .dataWidth(6)) rom_2 (.addr(counter_1_out_3), .data(out_4), .sel(I));
  ROM #(.addrWidth(2), .dataWidth(6)) rom_3 (.addr(counter_1_out_3), .data(out_5), .sel(I));
  ROM #(.addrWidth(2), .dataWidth(6)) rom_4 (.addr(counter_1_out_3), .data(out_6), .sel(I));
  ROM #(.addrWidth(2), .dataWidth(6)) rom_5 (.addr(counter_1_out_3), .data(out_7), .sel(I));
  ROM #(.addrWidth(2), .dataWidth(6)) rom_6 (.addr(counter_1_out_3), .data(out_8), .sel(I));
  ROM #(.addrWidth(2), .dataWidth(6)) rom_7 (.addr(counter_1_out_3), .data(out_9), .sel(I));
  ROM #(.addrWidth(2), .dataWidth(6)) rom_8 (.addr(counter_1_out_3), .data(out_10), .sel(I));
  ROM #(.addrWidth(2), .dataWidth(6)) rom_9 (.addr(counter_1_out_3), .data(out_11), .sel(I));
  ROM #(.addrWidth(2), .dataWidth(6)) rom_10 (.addr(counter_1_out_3), .data(out_12), .sel(I));
  ROM #(.addrWidth(2), .dataWidth(6)) rom_11 (.addr(counter_1_out_3), .data(out_13), .sel(I));
  ROM #(.addrWidth(2), .dataWidth(6)) rom_12 (.addr(counter_1_out_3), .data(out_14), .sel(I));
  ROM #(.addrWidth(2), .dataWidth(6)) rom_13 (.addr(counter_1_out_3), .data(out_15), .sel(I));
  ROM #(.addrWidth(2), .dataWidth(6)) rom_14 (.addr(counter_1_out_3), .data(out_16), .sel(I));
  ROM #(.addrWidth(2), .dataWidth(6)) rom_15 (.addr(counter_1_out_3), .data(out_17), .sel(I));
  ROM #(.addrWidth(2), .dataWidth(6)) rom_16 (.addr(counter_1_out_3), .data(out_18), .sel(I));
  ROM #(.addrWidth(2), .dataWidth(6)) rom_17 (.addr(counter_1_out_3), .data(out_19), .sel(I));
  ROM #(.addrWidth(2), .dataWidth(6)) rom_18 (.addr(counter_1_out_3), .data(out_20), .sel(I));
  ROM #(.addrWidth(2), .dataWidth(6)) rom_19 (.addr(counter_1_out_3), .data(out_21), .sel(I));
  ROM #(.addrWidth(2), .dataWidth(6)) rom_20 (.addr(counter_1_out_3), .data(out_22), .sel(I));
  ROM #(.addrWidth(2), .dataWidth(6)) rom_21 (.addr(counter_1_out_3), .data(out_23), .sel(I));
  ROM #(.addrWidth(2), .dataWidth(6)) rom_22 (.addr(counter_1_out_3), .data(out_24), .sel(I));
  ROM #(.addrWidth(2), .dataWidth(6)) rom_23 (.addr(counter_1_out_3), .data(out_25), .sel(I));
  ROM #(.addrWidth(2), .dataWidth(6)) rom_24 (.addr(counter_1_out_3), .data(out_26), .sel(I));
  ROM #(.addrWidth(2), .dataWidth(6)) rom_25 (.addr(counter_1_out_3), .data(out_27), .sel(I));
  ROM #(.addrWidth(2), .dataWidth(6)) rom_26 (.addr(counter_1_out_3), .data(out_28), .sel(I));
  ROM #(.addrWidth(2), .dataWidth(6)) rom_27 (.addr(counter_1_out_3), .data(out_29), .sel(I));
  ROM #(.addrWidth(2), .dataWidth(6)) rom_28 (.addr(counter_1_out_3), .data(out_30), .sel(I));
  ROM #(.addrWidth(2), .dataWidth(6)) rom_29 (.addr(counter_1_out_3), .data(out_31), .sel(I));
  ROM #(.addrWidth(2), .dataWidth(6)) rom_30 (.addr(counter_1_out_3), .data(out_32), .sel(I));
  ROM #(.addrWidth(2), .dataWidth(6)) rom_31 (.addr(counter_1_out_3), .data(out_33), .sel(I));
  ROM #(.addrWidth(2), .dataWidth(6)) rom_32 (.addr(counter_1_out_3), .data(out_34), .sel(I));
  ROM #(.addrWidth(2), .dataWidth(6)) rom_33 (.addr(counter_1_out_3), .data(out_35), .sel(I));
  ROM #(.addrWidth(2), .dataWidth(6)) rom_34 (.addr(counter_1_out_3), .data(out_36), .sel(I));
  ROM #(.addrWidth(2), .dataWidth(6)) rom_35 (.addr(counter_1_out_3), .data(out_37), .sel(I));
  ROM #(.addrWidth(2), .dataWidth(6)) rom_36 (.addr(counter_1_out_3), .data(out_38), .sel(I));
  ROM #(.addrWidth(2), .dataWidth(6)) rom_37 (.addr(counter_1_out_3), .data(out_39), .sel(I));
  ROM #(.addrWidth(2), .dataWidth(6)) rom_38 (.addr(counter_1_out_3), .data(out_40), .sel(I));
  ROM #(.addrWidth(2), .dataWidth(6)) rom_39 (.addr(counter_1_out_3), .data(out_41), .sel(I));
  ROM #(.addrWidth(2), .dataWidth(6)) rom_40 (.addr(counter_1_out_3), .data(out_42), .sel(I));
endmodule

// And
module Controller (
  input  A,
  input  A_2,
  output out_3
);

  wire comparator_1_gt, comparator_2_gt;

  Comparator #(.width(1)) comparator_1 (.a(A), .b(1'b1), .gt(comparator_1_gt));  // open: eq, lt
  Comparator #(.width(1)) comparator_2 (.a(A_2), .b(1'b1), .gt(comparator_2_gt));  // open: eq, lt
  and and_1 (out_3, comparator_1_gt, comparator_2_gt);
endmodule
